# Fritzing sketch Schematic (saved by Fritzing 0.9.3b)

parts:
  Componente1 = Arduino Nano (Rev3.0)
  Nokia_5110_LCD_Module1 = Nokia 5110 LCD
  R2 = Resistor [tolerance=±5% resistance=220 package=THT]
  R3 = Resistor [tolerance=±5% resistance=220 package=THT]
  R4 = Resistor [tolerance=±5% resistance=220 package=THT]
  R5 = Resistor [tolerance=±5% resistance=220 package=THT]
  R6 = Resistor [tolerance=±5% resistance=220 package=THT]
  M1 = DC Motor  # not connected
  R7 = Rotary Potentiometer (Small) [maximum_resistance=100kΩ package=THT]
  J1 = Power Jack [package=power_jack_combo]
  S1 = H-Bridge with L298N

nets:
  GND: Componente1.GND, Nokia_5110_LCD_Module1.DN(MOSI), Nokia_5110_LCD_Module1.DN(MODI)_(out), R7.leg2, J1.GNDBREAK, S1.GND
  N1: Componente1.D10, Nokia_5110_LCD_Module1.SCLK
  VIN: Componente1.VIN, J1.PWR, S1.12V
  N2: Componente1.RESET, Componente1.5V, Nokia_5110_LCD_Module1.LED, R7.leg1
  N3: Componente1.A0, R7.wiper
  N4: Nokia_5110_LCD_Module1.VCC, R6.Pin_1
  N5: Nokia_5110_LCD_Module1.GND, R2.Pin_1
  N6: Nokia_5110_LCD_Module1.SCE, R3.Pin_1
  N7: Nokia_5110_LCD_Module1.RST, R4.Pin_1
  N8: Nokia_5110_LCD_Module1.D/C, R5.Pin_1

custom parts:
  Nokia 5110 LCD: Nokia 5110 Graphic 84*48 LCD module such as the Sparkfun LCD-10168 or the clones from Ebay. There is example code for the Arduino available from the Sparkfun site in https://learn.sparkfun.com/tutorials/graphic-lcd-hookup-guide This is a 3.3V device, if you are running it from a 5V micro you need a 5V tolorant level translator such as the 74ahc367 to protect the signal imputs. Rafa G. did a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
  H-Bridge with L298N: h-bridge
